# Fritzing sketch environment-monitoring-wifi (saved by Fritzing 0.9.3b)
breadboards: 1

parts:
  WeMos_D1_Mini1 = WeMos D1 Mini
  VCC1 = Battery
  DHT1 = DHT22 Humidity and Temperature Sensor
  R1 = Resistor [tolerance=±5% resistance=10k package=THT]

nets:
  N1: WeMos_D1_Mini1.5V, VCC1.+, R1.Pin_1
  N2: WeMos_D1_Mini1.D0, WeMos_D1_Mini1.RST
  N3: WeMos_D1_Mini1.D5, DHT1.VDD
  N4: WeMos_D1_Mini1.D6, DHT1.DATA, R1.Pin_0
  N5: WeMos_D1_Mini1.G, VCC1.-, DHT1.GND

notes:
  6x 1.2 V or USB charger
  DHT22 Humidity & Temperature Sensor

custom parts:
  WeMos D1 Mini: The D1 mini is a mini wifi board based on ESP-8266EX.
