# Fritzing sketch pot-monitoring-wifi (saved by Fritzing 0.9.3b)
breadboards: 1

parts:
  WeMos_D1_Mini1 = WeMos D1 Mini
  Part1 = Soil Moisture Sensor
  Part2 = FC-28 Soil Hygrometer Module
  VCC1 = Battery

nets:
  N1: WeMos_D1_Mini1.5V, VCC1.+
  N2: WeMos_D1_Mini1.A0, Part2.AO
  N3: WeMos_D1_Mini1.D0, WeMos_D1_Mini1.RST
  N4: WeMos_D1_Mini1.D5, Part2.VCC
  N5: WeMos_D1_Mini1.G, Part2.GND, VCC1.-
  N6: Part1.GND, Part2.NEG
  N7: Part1.VCC, Part2.POS

notes:
  6x 1.2 V or USB charger

custom parts:
  WeMos D1 Mini: The D1 mini is a mini wifi board based on ESP-8266EX.
  FC-28 Soil Hygrometer Module: The FC-28 is a soil hygrometer module that uses the Texas Instruments LM393 comparator chip to provide an analog measurement of soil humidity. The digital output is high when soil moisture is over a certain threshold, as determined by adjusting the potentiometer.
